// Logisim project cpu.circ as structural Verilog: 1 circuit, main circuit main
// 1
module main (
  input  [31:0] INSTRUCTION,
  input  CLOCK,
  output [31:0] FETCH_ADDRESS,
  output [31:0] s0_Value,
  output [31:0] s1_Value,
  output [31:0] s2_Value,
  output [31:0] ra_Value,
  output [31:0] sp_Value
);

  wire add, addi, addiu, addu, ALUSrc, \and , andi, beq, bltzal, bne, Branch, check, isJump, isOp1, isOp2,
       isR, isR1, isR2, j, jal, jr, Jump, lui, lw, MemWrite, not_1_out, not_2_out, not_4_out, \or , or_6_out,
       or_7_out, or_8_out, or_9_out, or_10_out, or_11_out, ori, RegWrite, sll, slt, slti, sltiu, sltu, sra,
       srl;
  wire [3:0] ALUOP, multiplexer_2_out, multiplexer_3_out, multiplexer_4_out, multiplexer_5_out,
       multiplexer_6_out, multiplexer_7_out, multiplexer_8_out, multiplexer_9_out;
  wire [4:0] demultiplexer_1_out0, demultiplexer_1_out1, demultiplexer_2_out0, demultiplexer_2_out1,
       multiplexer_10_out;
  wire [31:0] adder_1_out, and_2_out, jAddr, multiplexer_1_out, PC, preAddr;

  Demultiplexer #(.width(5)) demultiplexer_1 (
    .out0(demultiplexer_1_out0), .out1(demultiplexer_1_out1), .in(INSTRUCTION[4:0]), .sel(INSTRUCTION[5]),
    .en(isR));
  and and_1 (isR2, INSTRUCTION[5], isR);
  Multiplexer #(.width(32), .enable("false")) multiplexer_1 (
    .in0(adder_1_out), .in1(jAddr), .out(multiplexer_1_out), .sel(isJump));
  Register #(.width(32)) u_PC (.D(multiplexer_1_out), .Q(PC), .clk(CLOCK));  // open: en, clr
  assign and_2_out = PC & 32'hf0000000;  // AND_Gate and_2, 32 bits wide
  assign jAddr = and_2_out | {preAddr[31:28], INSTRUCTION[25:0], preAddr[1:0]};  // OR_Gate or_1, 32 bits wide
  Comparator #(.width(6)) comparator_1 (.a(INSTRUCTION[31:26]), .b({6{1'b0}}), .eq(isR));  // open: gt, lt
  Decoder #(.select(5), .disabled(0)) decoder_1 (
    .out0(sll), .out2(srl), .out3(sra), .out8(jr), .out20(add), .out21(addu), .sel(demultiplexer_1_out0),
    .en(isR1));  // open: out1, out4, out5, out6, out7, out9, out10, out11, out12, out13, out14, out15, out16, out17, out18, out19, out22, out23, out24, out25, out26, out27, out28, out29, out30, out31
  not not_1 (not_1_out, isR2);
  and and_3 (isR1, not_1_out, isR);
  Adder #(.width(32)) adder_1 (.a(PC), .b(32'h4), .out(adder_1_out));  // open: cin, cout
  Decoder #(.select(5), .disabled(0)) decoder_2 (
    .out0(\and ), .out5(\or ), .out10(slt), .out11(sltu), .sel(demultiplexer_1_out1), .en(isR2));  // open: out1, out2, out3, out4, out6, out7, out8, out9, out12, out13, out14, out15, out16, out17, out18, out19, out20, out21, out22, out23, out24, out25, out26, out27, out28, out29, out30, out31
  Demultiplexer #(.width(5)) demultiplexer_2 (
    .out0(demultiplexer_2_out0), .out1(demultiplexer_2_out1), .in(INSTRUCTION[30:26]), .sel(INSTRUCTION[31]),
    .en(not_2_out));
  and and_4 (isOp2, INSTRUCTION[31], not_2_out);
  not not_2 (not_2_out, isR);
  not not_3 (ALUSrc, isR);
  Decoder #(.select(5), .disabled(0)) decoder_3 (
    .out1(bltzal), .out2(j), .out3(jal), .out4(beq), .out5(bne), .out8(addi), .out9(addiu), .out10(slti),
    .out11(sltiu), .out12(andi), .out13(ori), .out15(lui), .sel(demultiplexer_2_out0), .en(isOp1));  // open: out0, out6, out7, out14, out16, out17, out18, out19, out20, out21, out22, out23, out24, out25, out26, out27, out28, out29, out30, out31
  and and_5 (isOp1, isOp2, not_4_out);
  not not_4 (not_4_out, isR);
  or or_2 (check, beq, bne);
  or or_3 (Jump, jr, jal, j);
  or or_4 (RegWrite, srl, sll, sra, add, addu, sltu, sltiu, \or , slt, slti, \and , andi, ori, lui, lw, addiu);
  or or_5 (Branch, beq, bltzal, bne);
  Decoder #(.select(5), .disabled(0)) decoder_4 (
    .out3(lw), .out11(MemWrite), .sel(demultiplexer_2_out1), .en(isOp2));  // open: out0, out1, out2, out4, out5, out6, out7, out8, out9, out10, out12, out13, out14, out15, out16, out17, out18, out19, out20, out21, out22, out23, out24, out25, out26, out27, out28, out29, out30, out31
  or or_6 (or_6_out, addu, addiu);
  or or_7 (or_7_out, add, addi);
  or or_8 (or_8_out, \and , andi);
  or or_9 (or_9_out, \or , ori);
  or or_10 (or_10_out, slti, slt);
  or or_11 (or_11_out, sltiu, sltu);
  Multiplexer #(.width(4), .disabled(0), .enable("false")) multiplexer_2 (
    .in0(4'b0000), .in1(4'b0001), .out(multiplexer_2_out), .sel(srl));
  Multiplexer #(.width(4), .disabled(0), .enable("false")) multiplexer_3 (
    .in0(4'b0000), .in1(4'b0010), .out(multiplexer_3_out), .sel(sra));
  Multiplexer #(.width(4), .disabled(0), .enable("false")) multiplexer_4 (
    .in0(4'b0000), .in1(4'b0110), .out(multiplexer_4_out), .sel(or_6_out));
  Multiplexer #(.width(4), .disabled(0), .enable("false")) multiplexer_5 (
    .in0(4'b0000), .in1(4'b0101), .out(multiplexer_5_out), .sel(or_7_out));
  Multiplexer #(.width(4), .disabled(0), .enable("false")) multiplexer_6 (
    .in0(4'b0000), .in1(4'b1001), .out(multiplexer_6_out), .sel(or_8_out));
  Multiplexer #(.width(4), .disabled(0), .enable("false")) multiplexer_7 (
    .in0(4'b0000), .in1(4'b1010), .out(multiplexer_7_out), .sel(or_9_out));
  Multiplexer #(.width(4), .disabled(0), .enable("false")) multiplexer_8 (
    .in0(4'b0000), .in1(4'b1110), .out(multiplexer_8_out), .sel(or_10_out));
  Multiplexer #(.width(4), .disabled(0), .enable("false")) multiplexer_9 (
    .in0(4'b0000), .in1(4'b1111), .out(multiplexer_9_out), .sel(or_11_out));
  assign ALUOP = multiplexer_2_out | multiplexer_3_out | multiplexer_4_out | multiplexer_5_out | multiplexer_6_out | multiplexer_7_out | multiplexer_8_out | multiplexer_9_out;  // OR_Gate or_12, 4 bits wide
  Multiplexer #(.width(5), .disabled(0), .enable("false")) multiplexer_10 (
    .in0(INSTRUCTION[20:16]), .in1(INSTRUCTION[15:11]), .out(multiplexer_10_out), .sel(isR));
  regfile_main main_1 (
    .Read_Register_1(INSTRUCTION[25:21]), .Read_Register_2(INSTRUCTION[20:16]),
    .Write_Register(multiplexer_10_out), .Write_Enable(RegWrite), .Clock(CLOCK), .s0_Value(s0_Value),
    .s1_Value(s1_Value), .s2_Value(s2_Value), .ra_Value(ra_Value), .sp_Value(sp_Value));  // open: Write_Data, Read_Data_1, Read_Data_2
  // mem_main main_2: pin names not known; wires that end beside it: MemWrite, CLOCK
  alu_main main_3 (.Switch(ALUOP));  // open: X, Equal, Result, Signed_Overflow, Y

  // Other names for the same wires on the sheet: clk = CLOCK; fetch_addr[31:0] = FETCH_ADDRESS;
  //   op[5:0] = INSTRUCTION[31:26]; RegDest = isR; MemRead = lw; MemToReg = lw; funct[5:0] = INSTRUCTION[5:0];
  //   immediate[15:0] = INSTRUCTION[15:0]; preAddr[27:2] = INSTRUCTION[25:0];
  //   SEI[31:0] = {{17{INSTRUCTION[15]}}, INSTRUCTION[14:0]}; shamt[4:0] = INSTRUCTION[10:6];
  //   rd[4:0] = INSTRUCTION[15:11]; rt[4:0] = INSTRUCTION[20:16]; rs[4:0] = INSTRUCTION[25:21]; ra[31:0] = ra_Value;
  //   s0[31:0] = s0_Value; s1[31:0] = s1_Value; s2[31:0] = s2_Value; sp[31:0] = sp_Value; sw = MemWrite

  // Notes on the sheet:
  //   Output
  //   These are outputs/inputs from run.circ
  //   Inputs
  //   These are DEBUG/TEST outputs from your circuit.
endmodule
